# Fritzing sketch Schema (saved by Fritzing 0.9.3b)
breadboards: 2

parts:
  LED1 = smd LED [color="Red (635nm)" package="1206 [SMD]"]
  R1 = Resistor [tolerance=±5% resistance=220 package="0603 [SMD]"]
  LED2 = smd LED [color="Yellow (595nm)" package="1206 [SMD]"]
  LED3 = smd LED [color="Green (555nm)" package="1206 [SMD]"]
  R2 = Resistor [tolerance=±5% resistance=220 package="0603 [SMD]"]
  R3 = Resistor [tolerance=±5% resistance=220 package="0603 [SMD]"]
  LED4 = smd LED [color="Blue (430nm)" package="1206 [SMD]"]
  R4 = Resistor [tolerance=±5% resistance=220 package="0603 [SMD]"]
  Part1 = Arduino Uno (Rev3)
  Part2 = KY-022 Infrared Receiver Module [package="Breakout board"]

nets:
  N1: LED1.cathode, LED2.cathode, LED3.cathode, LED4.cathode, Part1.GND, Part2.-
  N2: LED1.anode, R1.Pin_1
  N3: R1.Pin_0, Part1.D8
  N4: LED2.anode, R2.Pin_1
  N5: LED3.anode, R3.Pin_1
  N6: R2.Pin_0, Part1.D9_PWM
  N7: R3.Pin_0, Part1.D10_PWM/SS
  N8: LED4.anode, R4.Pin_1
  N9: R4.Pin_0, Part1.D11_PWM/MOSI
  N10: Part1.D2, Part2.S
  5V: Part1.5V, Part2.Vin

custom parts:
  KY-022 Infrared Receiver Module: Arduino IR receiver module KY-022, reacts to 38kHz infrared light.
